# Fritzing sketch at-me (saved by Fritzing 0.9.5d)
circuit board: 5.80035cm x 5.24737cm
breadboards: 1

parts:
  Arduino_Nano = Arduino Nano (Rev3.0)
  DFRobot_DFPlayer_Mini1 = DFRobot DFPlayer Mini [part_number=DFR0299]
  R11 = Resistor [tolerance=±5% resistance=1k package=THT]
  R2 = Resistor [tolerance=±5% resistance=220 package=THT]
  R3 = Resistor [tolerance=±5% resistance=10k package=THT]
  R5 = Resistor [tolerance=±5% resistance=220 package=THT]
  R4 = Resistor [tolerance=±5% resistance=10k package=THT]
  Speakers = female pin header, 2 pins [form="♀ (female)"]
  LED_Power = female pin header, 2 pins [form="♀ (female)"]
  LED_Shock = female pin header, 2 pins [form="♀ (female)"]
  Placche = female pin header, 2 pins [form="♀ (female)"]
  Shock_Deliver = female pin header, 2 pins [form="♀ (female)"]
  Poweron = female pin header, 2 pins [form="♀ (female)"]

nets:
  N1: Arduino_Nano.GND, DFRobot_DFPlayer_Mini1.GND-1, DFRobot_DFPlayer_Mini1.GND-2, R3.Pin_1, R4.Pin_0, LED_Power.pin2, LED_Shock.pin2, Poweron.pin2
  N2: Arduino_Nano.D2, R2.Pin_0
  N3: Arduino_Nano.D3, R3.Pin_0, Placche.pin2
  N4: Arduino_Nano.D4, R4.Pin_1, Shock_Deliver.pin2
  N5: Arduino_Nano.D5, R5.Pin_0
  N6: Arduino_Nano.D6, Poweron.pin1
  N7: Arduino_Nano.D10, DFRobot_DFPlayer_Mini1.TX
  N8: Arduino_Nano.D11/MOSI, R11.Pin_1
  5V: Arduino_Nano.5V, DFRobot_DFPlayer_Mini1.VCC, Placche.pin1, Shock_Deliver.pin1
  N9: DFRobot_DFPlayer_Mini1.RX, R11.Pin_0
  N10: DFRobot_DFPlayer_Mini1.SPK_1, Speakers.pin1
  N11: DFRobot_DFPlayer_Mini1.SPK_2, Speakers.pin2
  N12: R2.Pin_1, LED_Power.pin1
  N13: R5.Pin_1, LED_Shock.pin1

notes:
  AT-ME v.0.1
